// Logisim project 其他类型文件.circ as structural Verilog
module \实验一  (
  input  in1,
  input  in2,
  input  in3,
  input  in4,
  input  in5,
  output out1,
  output out2,
  output out3,
  output out4,
  output out5
);

  or or_1 (out1, in1, in2, in3, in4, in5);
  or or_2 (out2, in2, in3, in4, in5);
  or or_3 (out3, in3, in4, in5);
  or or_4 (out4, in4, in5);

  assign out5 = in5;
endmodule

module \测试电路  (
);

  wire _1_out, _2_out, _3_out, _4_out, _5_out, \实验一_1_out1 , \实验一_1_out2 , \实验一_1_out3 , \实验一_1_out4 ,
       \实验一_1_out5 ;

  Button _1 (.out(_1_out));
  Button _2 (.out(_2_out));
  Button _3 (.out(_3_out));
  Button _4 (.out(_4_out));
  Button _5 (.out(_5_out));
  \实验一  \u_实验一_1  (
    .in1(_1_out), .out1(\实验一_1_out1 ), .in2(_2_out), .out2(\实验一_1_out2 ), .in3(_3_out), .out3(\实验一_1_out3 ),
    .in4(_4_out), .out4(\实验一_1_out4 ), .in5(_5_out), .out5(\实验一_1_out5 ));
  LED #(.active("true")) led_1 (.in(\实验一_1_out1 ));
  LED #(.active("true")) led_2 (.in(\实验一_1_out2 ));
  LED #(.active("true")) led_3 (.in(\实验一_1_out3 ));
  LED #(.active("true")) led_4 (.in(\实验一_1_out4 ));
  LED #(.active("true")) led_5 (.in(\实验一_1_out5 ));
endmodule

module \_5输入电路  (
  input  In1,
  input  In2,
  input  In3,
  input  In4,
  input  In5,
  output Out1,
  output Out2,
  output Out3
);

  wire and_1_out, and_2_out, and_3_out, and_4_out, not_1_out, not_2_out, not_3_out, not_4_out, not_5_out,
       not_6_out, not_7_out;

  not not_1 (not_1_out, In4);
  not not_2 (not_2_out, In2);
  not not_3 (not_3_out, In4);
  not not_4 (not_4_out, In4);
  not not_5 (not_5_out, In5);
  not not_6 (not_6_out, In4);
  not not_7 (not_7_out, In5);
  or or_1 (Out3, In5, In4);
  and and_1 (and_1_out, In3, not_1_out);
  and and_2 (and_2_out, In1, not_2_out, not_3_out);
  and and_3 (and_3_out, In3, not_4_out, not_5_out);
  and and_4 (and_4_out, In2, not_6_out, not_7_out);
  or or_2 (Out1, In5, and_1_out, and_2_out);
  or or_3 (Out2, and_3_out, and_4_out);
endmodule

module \_5输入电路测试  (
);

  wire _1_out, _2_out, _3_out, _4_out, _5_out, \实验一_1_out1 , \实验一_1_out2 , \实验一_1_out3 , \实验一_1_out4 ,
       \实验一_1_out5 ;
  wire [2:0] \n5输入电路_1_out1 ;

  Button _1 (.out(_1_out));
  Button _2 (.out(_2_out));
  Button _3 (.out(_3_out));
  Button _4 (.out(_4_out));
  Button _5 (.out(_5_out));
  \实验一  \u_实验一_1  (
    .in1(_1_out), .out1(\实验一_1_out1 ), .in2(_2_out), .out2(\实验一_1_out2 ), .in3(_3_out), .out3(\实验一_1_out3 ),
    .in4(_4_out), .out4(\实验一_1_out4 ), .in5(_5_out), .out5(\实验一_1_out5 ));
  \_5输入电路  \u_5输入电路_1  (
    .In1(_1_out), .In2(_2_out), .In3(_3_out), .In4(_4_out), .In5(_5_out), .Out1(\n5输入电路_1_out1 [0]),
    .Out2(\n5输入电路_1_out1 [1]), .Out3(\n5输入电路_1_out1 [2]));
  LED #(.active("true")) led_1 (.in(\实验一_1_out1 ));
  LED #(.active("true")) led_2 (.in(\实验一_1_out2 ));
  LED #(.active("true")) led_3 (.in(\实验一_1_out3 ));
  LED #(.active("true")) led_4 (.in(\实验一_1_out4 ));
  LED #(.active("true")) led_5 (.in(\实验一_1_out5 ));
  Hex_Digit_Display hex_digit_display_1 (.value({1'b0, \n5输入电路_1_out1 }), .dp(1'b1));
endmodule

module \_7段数码管  (
  input  x1,
  input  x2,
  input  x3,
  input  x4,
  output a1,
  output a2,
  output a3,
  output a4,
  output a5,
  output a6,
  output a7
);

  wire and_1_out, and_2_out, and_3_out, and_4_out, and_5_out, and_6_out, and_7_out, and_8_out, and_9_out,
       and_10_out, and_11_out, and_12_out, and_13_out, and_14_out, and_15_out, and_16_out, and_17_out,
       and_18_out, and_19_out, and_20_out, and_21_out, and_22_out, and_23_out, and_24_out, and_25_out,
       and_26_out, and_27_out, and_28_out, and_29_out, and_30_out, and_31_out, and_32_out, and_33_out,
       and_34_out, not_1_out, not_2_out, not_3_out, not_4_out, not_5_out, not_6_out, not_7_out, not_8_out,
       not_9_out, not_10_out, not_11_out, not_12_out, not_13_out, not_14_out, not_15_out, not_16_out,
       not_17_out, not_18_out, not_19_out, not_20_out, not_21_out, not_22_out, not_23_out, not_24_out,
       not_25_out, not_26_out, not_27_out, not_28_out, not_29_out, not_30_out, not_31_out, not_32_out,
       not_33_out, not_34_out, not_35_out, not_36_out, not_37_out, not_38_out, not_39_out, not_40_out;

  not not_1 (not_1_out, x3);
  and and_1 (and_1_out, not_1_out, x4);
  not not_2 (not_2_out, x2);
  and and_2 (and_2_out, not_2_out, x3, not_3_out);
  not not_3 (not_3_out, x4);
  not not_4 (not_4_out, x1);
  and and_3 (and_3_out, not_4_out, x2);
  and and_4 (and_4_out, x2, not_5_out);
  not not_5 (not_5_out, x3);
  and and_5 (and_5_out, x1, x4);
  not not_6 (not_6_out, x1);
  and and_6 (and_6_out, not_6_out, not_7_out);
  not not_7 (not_7_out, x2);
  not not_8 (not_8_out, x1);
  and and_7 (and_7_out, not_8_out, x3);
  not not_9 (not_9_out, x2);
  and and_8 (and_8_out, not_9_out, x3);
  and and_9 (and_9_out, x1, x4);
  not not_10 (not_10_out, x1);
  and and_10 (and_10_out, not_10_out, not_11_out);
  not not_11 (not_11_out, x3);
  not not_12 (not_12_out, x1);
  and and_11 (and_11_out, not_12_out, x4);
  not not_13 (not_13_out, x2);
  and and_12 (and_12_out, not_13_out, not_14_out, x4);
  not not_14 (not_14_out, x3);
  and and_13 (and_13_out, x2, not_15_out);
  not not_15 (not_15_out, x4);
  and and_14 (and_14_out, x2, x3);
  and and_15 (and_15_out, x1, x3, not_16_out);
  not not_16 (not_16_out, x4);
  not not_17 (not_17_out, x1);
  and and_16 (and_16_out, not_17_out, not_18_out, not_19_out);
  not not_18 (not_18_out, x2);
  not not_19 (not_19_out, x4);
  not not_20 (not_20_out, x1);
  and and_17 (and_17_out, not_20_out, not_21_out);
  not not_21 (not_21_out, x3);
  not not_22 (not_22_out, x2);
  and and_18 (and_18_out, not_22_out, not_23_out);
  not not_23 (not_23_out, x3);
  not not_24 (not_24_out, x1);
  and and_19 (and_19_out, not_24_out, x2, x4);
  and and_20 (and_20_out, x1, x2, not_25_out);
  not not_25 (not_25_out, x4);
  not not_26 (not_26_out, x1);
  and and_21 (and_21_out, not_26_out, not_27_out);
  not not_27 (not_27_out, x3);
  and and_22 (and_22_out, x3, x4);
  not not_28 (not_28_out, x1);
  and and_23 (and_23_out, not_28_out, x2);
  and and_24 (and_24_out, x2, x4);
  not not_29 (not_29_out, x1);
  and and_25 (and_25_out, not_29_out, not_30_out);
  not not_30 (not_30_out, x3);
  not not_31 (not_31_out, x2);
  and and_26 (and_26_out, not_31_out, x4);
  not not_32 (not_32_out, x1);
  and and_27 (and_27_out, not_32_out, x2);
  and and_28 (and_28_out, x2, not_33_out);
  not not_33 (not_33_out, x3);
  and and_29 (and_29_out, x1, not_34_out, x3);
  not not_34 (not_34_out, x2);
  not not_35 (not_35_out, x2);
  and and_30 (and_30_out, not_35_out, not_36_out);
  not not_36 (not_36_out, x3);
  not not_37 (not_37_out, x3);
  and and_31 (and_31_out, not_37_out, x4);
  and and_32 (and_32_out, x3, not_38_out);
  not not_38 (not_38_out, x4);
  and and_33 (and_33_out, x1, not_39_out);
  not not_39 (not_39_out, x2);
  and and_34 (and_34_out, x1, not_40_out);
  not not_40 (not_40_out, x3);
  or or_1 (a1, and_1_out, and_2_out, and_3_out, and_4_out, and_5_out);
  or or_2 (a2, and_6_out, and_7_out, and_8_out, and_9_out);
  or or_3 (a4, and_16_out, and_17_out, and_18_out, and_19_out, and_20_out);
  or or_4 (a5, and_21_out, and_22_out, and_23_out, and_24_out);
  or or_5 (a6, and_25_out, and_26_out, and_27_out, and_28_out, and_29_out);
  or or_6 (a7, and_30_out, and_31_out, and_32_out, and_33_out, and_34_out);
  or or_7 (a3, and_10_out, and_11_out, and_12_out, and_13_out, and_14_out, and_15_out);
endmodule

module \_7段数码管测试  (
);

  wire clock_1_out, \n7段数码管_1_a1 , \n7段数码管_1_a2 , \n7段数码管_1_a3 , \n7段数码管_1_a4 , \n7段数码管_1_a5 , \n7段数码管_1_a6 ,
       \n7段数码管_1_a7 ;
  wire [3:0] counter_1_q;

  Counter #(.width(4), .max('hf), .ongoal("wrap"), .trigger("rising"), .behavior("new")) counter_1 (
    .Q(counter_1_q), .clk(clock_1_out));  // open: load, D, count, carry, clr, preset, down
  Clock #(.highDuration(1), .lowDuration(1)) clock_1 (.out(clock_1_out));
  \_7段数码管  \u_7段数码管_1  (
    .x1(counter_1_q[0]), .x2(counter_1_q[1]), .x3(counter_1_q[2]), .x4(counter_1_q[3]), .a1(\n7段数码管_1_a1 ),
    .a2(\n7段数码管_1_a2 ), .a3(\n7段数码管_1_a3 ), .a4(\n7段数码管_1_a4 ), .a5(\n7段数码管_1_a5 ), .a6(\n7段数码管_1_a6 ),
    .a7(\n7段数码管_1_a7 ));
  _7_Segment_Display #(.active("true")) u_7_segment_display_1 (
    .g(\n7段数码管_1_a1 ), .f(\n7段数码管_1_a2 ), .a(\n7段数码管_1_a3 ), .b(\n7段数码管_1_a4 ), .e(\n7段数码管_1_a5 ),
    .d(\n7段数码管_1_a6 ), .c(\n7段数码管_1_a7 ));  // open: dp
endmodule

module \LED测试电路  (
);

  wire _1_out, _2_out, _3_out, _4_out, _5_out, \n7段数码管_1_a1 , \n7段数码管_1_a2 , \n7段数码管_1_a3 , \n7段数码管_1_a4 ,
       \n7段数码管_1_a5 , \n7段数码管_1_a6 , \n7段数码管_1_a7 , \实验一_1_out1 , \实验一_1_out2 , \实验一_1_out3 , \实验一_1_out4 ,
       \实验一_1_out5 ;
  wire [2:0] \n5输入电路_1_out1 ;

  Button _1 (.out(_1_out));
  Button _2 (.out(_2_out));
  Button _3 (.out(_3_out));
  Button _4 (.out(_4_out));
  Button _5 (.out(_5_out));
  \实验一  \u_实验一_1  (
    .in1(_1_out), .out1(\实验一_1_out1 ), .in2(_2_out), .out2(\实验一_1_out2 ), .in3(_3_out), .out3(\实验一_1_out3 ),
    .in4(_4_out), .out4(\实验一_1_out4 ), .in5(_5_out), .out5(\实验一_1_out5 ));
  \_5输入电路  \u_5输入电路_1  (
    .In1(_1_out), .In2(_2_out), .In3(_3_out), .In4(_4_out), .In5(_5_out), .Out1(\n5输入电路_1_out1 [0]),
    .Out2(\n5输入电路_1_out1 [1]), .Out3(\n5输入电路_1_out1 [2]));
  LED #(.active("true")) led_1 (.in(\实验一_1_out1 ));
  LED #(.active("true")) led_2 (.in(\实验一_1_out2 ));
  LED #(.active("true")) led_3 (.in(\实验一_1_out3 ));
  LED #(.active("true")) led_4 (.in(\实验一_1_out4 ));
  LED #(.active("true")) led_5 (.in(\实验一_1_out5 ));
  \_7段数码管  \u_7段数码管_1  (
    .x1(\n5输入电路_1_out1 [0]), .x2(\n5输入电路_1_out1 [1]), .x3(\n5输入电路_1_out1 [2]), .x4(1'b0), .a1(\n7段数码管_1_a1 ),
    .a2(\n7段数码管_1_a2 ), .a3(\n7段数码管_1_a3 ), .a4(\n7段数码管_1_a4 ), .a5(\n7段数码管_1_a5 ), .a6(\n7段数码管_1_a6 ),
    .a7(\n7段数码管_1_a7 ));
  // Probe on \n5输入电路_1_out1 
  Hex_Digit_Display hex_digit_display_1 (.value({1'b0, \n5输入电路_1_out1 }), .dp(1'b1));
  _7_Segment_Display #(.active("true")) u_7_segment_display_1 (
    .g(\n7段数码管_1_a1 ), .f(\n7段数码管_1_a2 ), .a(\n7段数码管_1_a3 ), .b(\n7段数码管_1_a4 ), .e(\n7段数码管_1_a5 ),
    .d(\n7段数码管_1_a6 ), .c(\n7段数码管_1_a7 ), .dp(1'b1));
endmodule
